# Fritzing sketch Circuit_Layout_Shoron (saved by Fritzing 0.9.3b)

parts:
  M1 = Mega2560 R3 Pro ch340g
  LED10 = RGB LED (com. cathode, rbg) [package="5 mm [THT]"]
  LED11 = RGB LED (com. cathode, rgb) [package="5 mm [THT]"]
  LED13 = RGB LED (com. anode, rbg) [package="5 mm [THT]"]
  LED14 = RGB LED (com. cathode, rbg) [package="5 mm [THT]"]
  LED15 = RGB LED (com. cathode, rgb) [package="5 mm [THT]"]
  LED17 = RGB LED (com. anode, rbg) [package="5 mm [THT]"]
  J1 = Piezo Speaker
  U1 = SWITCH_SPDT [package=kps-1290]
  S8 = Round Pushbutton
  S9 = Square Pushbutton
  ZS-042_RTC1 = ZS-042 RTC Module
  SIM800L1 = SIM800L
  U2 = LM2596 step down module
  BAT1 = BC9VPC [package=bc9vpc]
  R1 = Resistor [tolerance=±5% resistance=220 package=THT]
  R2 = Resistor [tolerance=±5% resistance=220 package=THT]
  R3 = Resistor [tolerance=±5% resistance=220 package=THT]
  R4 = Resistor [tolerance=±5% resistance=220 package=THT]
  R5 = Resistor [tolerance=±5% resistance=220 package=THT]
  R6 = Resistor [tolerance=±5% resistance=220 package=THT]
  R7 = Resistor [tolerance=±5% resistance=220 package=THT]
  R8 = Resistor [tolerance=±5% resistance=220 package=THT]
  R9 = Resistor [tolerance=±5% resistance=220 package=THT]
  R10 = Resistor [tolerance=±5% resistance=220 package=THT]
  R11 = Resistor [tolerance=±5% resistance=220 package=THT]
  R12 = Resistor [tolerance=±5% resistance=220 package=THT]
  LED21 = RGB LED (com. cathode, rgb) [package="5 mm [THT]"]
  LED22 = RGB LED (com. cathode, rgb) [package="5 mm [THT]"]
  LED23 = RGB LED (com. cathode, rgb) [package="5 mm [THT]"]
  LED24 = RGB LED (com. cathode, rgb) [package="5 mm [THT]"]
  LED25 = RGB LED (com. anode, rbg) [package="5 mm [THT]"]
  LED26 = RGB LED (com. anode, rbg) [package="5 mm [THT]"]
  R25 = Resistor [tolerance=±5% resistance=220 package=THT]
  R26 = Resistor [tolerance=±5% resistance=220 package=THT]
  R27 = Resistor [tolerance=±5% resistance=220 package=THT]
  R28 = Resistor [tolerance=±5% resistance=220 package=THT]
  R29 = Resistor [tolerance=±5% resistance=220 package=THT]
  R30 = Resistor [tolerance=±5% resistance=220 package=THT]
  R31 = Resistor [tolerance=±5% resistance=220 package=THT]
  R32 = Resistor [tolerance=±5% resistance=220 package=THT]
  R33 = Resistor [tolerance=±5% resistance=220 package=THT]
  R34 = Resistor [tolerance=±5% resistance=220 package=THT]
  R35 = Resistor [tolerance=±5% resistance=220 package=THT]
  R36 = Resistor [tolerance=±5% resistance=220 package=THT]
  S12 = Pushbutton [package="[SMD]"]
  S13 = Pushbutton [package="[SMD]"]
  S14 = Pushbutton [package="[THT]"]
  S15 = Pushbutton [package="[THT]"]

nets:
  N1: M1.40, J1.pin2
  N2: M1.38, R26.Pin_1
  N3: M1.36, R30.Pin_1
  N4: M1.34, R27.Pin_1
  N5: M1.32, R25.Pin_1
  N6: M1.A14, R29.Pin_1
  N7: M1.A12, R28.Pin_1
  N8: M1.A10, R32.Pin_1
  N9: M1.A8, R36.Pin_1
  N10: M1.A6, R33.Pin_1
  N11: M1.A4, R31.Pin_1
  N12: M1.A2, R35.Pin_1
  N13: M1.A0, R34.Pin_1
  N14: M1.3▀, S15.Pin_1
  N15: M1.5▀, R1.Pin_1
  N16: M1.7▀, R2.Pin_1
  N17: M1.9▀, R3.Pin_1
  N18: M1.11▀, R4.Pin_1
  N19: M1.13▀, R5.Pin_1
  N20: M1.15, R6.Pin_1
  N21: M1.17, SIM800L1.TXD
  N22: M1.19, S14.Pin_1
  N23: M1.21, ZS-042_RTC1.SCL
  N24: M1.23, S8.leg1
  N25: M1.25, S9.leg0
  N26: M1.24, U1.S
  N27: M1.22, U1.O
  N28: M1.20, ZS-042_RTC1.SDA
  N29: M1.18, S12.Pin_1, S12.Pin_2
  N30: M1.16, SIM800L1.RXD
  N31: M1.14, R9.Pin_1
  N32: M1.12▀, R10.Pin_1
  N33: M1.10▀, R12.Pin_1
  N34: M1.8▀, R8.Pin_1
  N35: M1.6▀, R7.Pin_1
  N36: M1.4▀, R11.Pin_1
  N37: M1.2▀, S13.Pin_1, S13.Pin_2
  N38: M1.Vin-1, M1.Vin-2, U2.IN+, BAT1.V+
  GND: M1.GND-1, M1.GND-2, ZS-042_RTC1.GND, SIM800L1.GND, U2.IN-, U2.OUT-, BAT1.V-, S13.Pin_3, S13.Pin_4
  N39: M1.5V-2, ZS-042_RTC1.VCC
  N40: LED10.red_anode, R9.Pin_0
  N41: LED10.blue_anode, R8.Pin_0
  N42: LED11.red_anode, R7.Pin_0
  N43: LED11.green_anode, R11.Pin_0
  N44: LED13.red_cathode, R12.Pin_0
  N45: LED13.blue_cathode, R10.Pin_0
  N46: LED14.red_anode, R1.Pin_0
  N47: LED14.blue_anode, R2.Pin_0
  N48: LED15.red_anode, R5.Pin_0
  N49: LED15.green_anode, R6.Pin_0
  N50: LED17.red_cathode, R3.Pin_0
  N51: LED17.blue_cathode, R4.Pin_0
  N52: SIM800L1.VCC, U2.OUT+
  N53: LED21.red_anode, R25.Pin_0
  N54: LED21.green_anode, R27.Pin_0
  N55: LED22.red_anode, R30.Pin_0
  N56: LED22.green_anode, R26.Pin_0
  N57: LED23.red_anode, R36.Pin_0
  N58: LED23.green_anode, R32.Pin_0
  N59: LED24.red_anode, R31.Pin_0
  N60: LED24.green_anode, R33.Pin_0
  N61: LED25.red_cathode, R28.Pin_0
  N62: LED25.blue_cathode, R29.Pin_0
  N63: LED26.red_cathode, R34.Pin_0
  N64: LED26.blue_cathode, R35.Pin_0

notes:
  Shoron_Circuit_Layout

custom parts:
  Mega2560 R3 Pro ch340g: The Mega 2560 R3 Pro Mini :- Completely compatible with original Arduino Mega2560 Pin pitch: 0.1 inch Size: 5.42cm*3.68cm With Atmega16U2 chip as the USB to Serial converter 5V working voltage. Input Voltage:7-12V Analog Input Pins: 16 Digital I/O pins: 54 The Mega 2560 R3 Pro Mini has no datasheet and no info and I don't have one to compare, so I made this based on photos. Dec 2019 modified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
  SIM800L: SIM800L is a miniature cellular module which allows for GPRS transmission, sending and receiving SMS and making and receiving voice calls. Low cost and small footprint and quad band frequency support make this module perfect solution for any project that require long range connectivity. After connecting power module boots up, searches for cellular network and login automatically. On board LED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
  LM2596 step down module: LM2596 DC-DC step down power supply module 3 A.
